// Logisim project oblArqui.circ as structural Verilog: 19 circuits, main circuit main
module main (
);

  wire and_1_out, contadorbin_1_led1, contadorbin_1_led2, contadorbin_1_led3, contadorbin_1_led4,
       contadorbin_1_led5, contadorbin_1_led6, contadorbin_1_led7, contadorbin_1_led8, contadorbin_1_led9,
       contadorbin_1_led10, d_ff_1_q, D_out, detectorfilacompleta_1_borrar, finpartida_1_col0_full,
       finpartida_1_col1_full, finpartida_1_col2_full, finpartida_1_col3_full, finpartida_1_col4_full,
       finpartida_1_fin, finpartida_1_reset, guardarnuevoestado_1_colisionder,
       guardarnuevoestado_1_colisionizq, guardarnuevoestado_1_colisiony, guardarnuevoestado_1_sumarpunto,
       I_out, manejovelocidades_1_salida, or_1_out, puntajerecord_1_led1, puntajerecord_1_led2,
       puntajerecord_1_led3, puntajerecord_1_led4, puntajerecord_1_led5, puntajerecord_1_led6,
       puntajerecord_1_led7, puntajerecord_1_led8, puntajerecord_1_led9, puntajerecord_1_led10, Reloj,
       Reset_out, Reset_Record_out, Start_out;
  wire [2:0] movimientocuadrado_1_colactual;
  wire [3:0] contador2_1_puntos1, contador2_1_puntos2, contador2_1_puntos3, contador2_1_puntos4,
       puntajerecordhexa_1_record1, puntajerecordhexa_1_record2, puntajerecordhexa_1_record3,
       puntajerecordhexa_1_record4;
  wire [4:0] movimientocuadrado_1_inicio;
  wire [7:0] detectorfilacompleta_1_nuevacol0, detectorfilacompleta_1_nuevacol1,
       detectorfilacompleta_1_nuevacol2, detectorfilacompleta_1_nuevacol3, detectorfilacompleta_1_nuevacol4,
       guardarnuevoestado_1_col_0, guardarnuevoestado_1_col_1, guardarnuevoestado_1_col_2,
       guardarnuevoestado_1_col_3, guardarnuevoestado_1_col_4, juntartableros_1_c0, juntartableros_1_c1,
       juntartableros_1_c2, juntartableros_1_c3, juntartableros_1_c4, movimientocuadrado_1_col0,
       movimientocuadrado_1_col1, movimientocuadrado_1_col2, movimientocuadrado_1_col3,
       movimientocuadrado_1_col4, movimientocuadrado_1_filaactual;

  Clock clock_1 (.out(Reloj));
  ManejoVelocidades manejovelocidades_1 (
    .clk(Reloj), .entrada(guardarnuevoestado_1_sumarpunto), .reset(or_1_out),
    .salida(manejovelocidades_1_salida));
  Button Start (.out(Start_out));
  Button Reset (.out(Reset_out));
  D_Flip_Flop d_ff_1 (.D(detectorfilacompleta_1_borrar), .clk(Reloj), .Q(d_ff_1_q));  // open: Qn, preset, reset
  contadorBin contadorbin_1 (
    .Entrada(guardarnuevoestado_1_sumarpunto), .Suma5(d_ff_1_q), .Reset(or_1_out), .Clock(Reloj),
    .Led1(contadorbin_1_led1), .Led2(contadorbin_1_led2), .Led3(contadorbin_1_led3),
    .Led4(contadorbin_1_led4), .Led5(contadorbin_1_led5), .Led6(contadorbin_1_led6),
    .Led7(contadorbin_1_led7), .Led8(contadorbin_1_led8), .Led9(contadorbin_1_led9),
    .Led10(contadorbin_1_led10));
  contador2 contador2_1 (
    .Reset(or_1_out), .Suma5(d_ff_1_q), .Sumar1(guardarnuevoestado_1_sumarpunto), .Clock(Reloj),
    .Puntos4(contador2_1_puntos4), .Puntos3(contador2_1_puntos3), .Puntos2(contador2_1_puntos2),
    .Puntos1(contador2_1_puntos1));
  Button Reset_Record (.out(Reset_Record_out));
  LED Col_Y (.in(guardarnuevoestado_1_colisiony));
  LED Col_Izq (.in(guardarnuevoestado_1_colisionizq));
  LED Col_Der (.in(guardarnuevoestado_1_colisionder));
  movimientoCuadrado movimientocuadrado_1 (
    .colisionY(guardarnuevoestado_1_colisiony), .strart(Start_out), .Clock(manejovelocidades_1_salida),
    .izq(I_out), .der(D_out), .colisionIzq(guardarnuevoestado_1_colisionizq),
    .colisionDer(guardarnuevoestado_1_colisionder), .reset(or_1_out), .inicio(movimientocuadrado_1_inicio),
    .col0(movimientocuadrado_1_col0), .col1(movimientocuadrado_1_col1), .col2(movimientocuadrado_1_col2),
    .col3(movimientocuadrado_1_col3), .col4(movimientocuadrado_1_col4),
    .filaActual(movimientocuadrado_1_filaactual), .colActual(movimientocuadrado_1_colactual));
  DotMatrix #(.matrixrows(1)) dotmatrix_1 (
    .col0(movimientocuadrado_1_inicio[4]), .col1(movimientocuadrado_1_inicio[3]),
    .col2(movimientocuadrado_1_inicio[2]), .col3(movimientocuadrado_1_inicio[1]),
    .col4(movimientocuadrado_1_inicio[0]));
  Button I (.out(I_out));
  DotMatrix #(.matrixrows(8)) dotmatrix_2 (
    .col0(juntartableros_1_c0), .col1(juntartableros_1_c1), .col2(juntartableros_1_c2),
    .col3(juntartableros_1_c3), .col4(juntartableros_1_c4));
  Button D (.out(D_out));
  Hex_Digit_Display hex_digit_display_1 (.value(contador2_1_puntos3));  // open: dp
  Hex_Digit_Display hex_digit_display_2 (.value(contador2_1_puntos4));  // open: dp
  PuntajeRecordHexa puntajerecordhexa_1 (
    .Puntos4(contador2_1_puntos4), .Puntos3(contador2_1_puntos3), .Puntos2(contador2_1_puntos2),
    .Puntos1(contador2_1_puntos1), .Reset(Reset_Record_out), .Clock(Reloj),
    .Record4(puntajerecordhexa_1_record4), .Record3(puntajerecordhexa_1_record3),
    .Record2(puntajerecordhexa_1_record2), .Record1(puntajerecordhexa_1_record1));
  Hex_Digit_Display hex_digit_display_3 (.value(contador2_1_puntos2));  // open: dp
  Hex_Digit_Display hex_digit_display_4 (.value(contador2_1_puntos1));  // open: dp
  or or_1 (or_1_out, finpartida_1_reset, Reset_out);
  LED led_1 (.in(contadorbin_1_led1));
  LED led_2 (.in(contadorbin_1_led2));
  guardarNuevoEstado guardarnuevoestado_1 (
    .BORRAR_FILA(detectorfilacompleta_1_borrar), .CLK(Reloj), .RESET(or_1_out),
    .WRITE_ENABLE(manejovelocidades_1_salida), .Y_POS(movimientocuadrado_1_filaactual),
    .X_POS(movimientocuadrado_1_colactual), .LOOP_C0(detectorfilacompleta_1_nuevacol0),
    .LOOP_C1(detectorfilacompleta_1_nuevacol1), .LOOP_C2(detectorfilacompleta_1_nuevacol2),
    .LOOP_C3(detectorfilacompleta_1_nuevacol3), .LOOP_C4(detectorfilacompleta_1_nuevacol4),
    .COL_0(guardarnuevoestado_1_col_0), .COL_1(guardarnuevoestado_1_col_1),
    .COL_2(guardarnuevoestado_1_col_2), .COL_3(guardarnuevoestado_1_col_3),
    .COL_4(guardarnuevoestado_1_col_4), .colisionY(guardarnuevoestado_1_colisiony),
    .colisionDer(guardarnuevoestado_1_colisionder), .colisionIzq(guardarnuevoestado_1_colisionizq),
    .SumarPunto(guardarnuevoestado_1_sumarpunto));
  LED led_3 (.in(contadorbin_1_led3));
  LED led_4 (.in(contadorbin_1_led4));
  LED led_5 (.in(contadorbin_1_led5));
  LED led_6 (.in(contadorbin_1_led6));
  LED led_7 (.in(contadorbin_1_led7));
  LED led_8 (.in(contadorbin_1_led8));
  LED led_9 (.in(contadorbin_1_led9));
  LED led_10 (.in(contadorbin_1_led10));
  Hex_Digit_Display hex_digit_display_5 (.value(puntajerecordhexa_1_record4));  // open: dp
  Hex_Digit_Display hex_digit_display_6 (.value(puntajerecordhexa_1_record3));  // open: dp
  Hex_Digit_Display hex_digit_display_7 (.value(puntajerecordhexa_1_record2));  // open: dp
  Hex_Digit_Display hex_digit_display_8 (.value(puntajerecordhexa_1_record1));  // open: dp
  LED led_11 (.in(puntajerecord_1_led1));
  LED led_12 (.in(puntajerecord_1_led2));
  LED led_13 (.in(puntajerecord_1_led3));
  finPartida finpartida_1 (
    .clk(Reloj), .col0(guardarnuevoestado_1_col_0), .col1(guardarnuevoestado_1_col_1),
    .col2(guardarnuevoestado_1_col_2), .col3(guardarnuevoestado_1_col_3), .col4(guardarnuevoestado_1_col_4),
    .reset(finpartida_1_reset), .fin(finpartida_1_fin), .COL0_FULL(finpartida_1_col0_full),
    .COL1_FULL(finpartida_1_col1_full), .COL2_FULL(finpartida_1_col2_full),
    .COL3_FULL(finpartida_1_col3_full), .COL4_FULL(finpartida_1_col4_full));
  LED led_14 (.in(puntajerecord_1_led4));
  LED led_15 (.in(puntajerecord_1_led5));
  LED led_16 (.in(puntajerecord_1_led6));
  LED led_17 (.in(puntajerecord_1_led7));
  LED led_18 (.in(puntajerecord_1_led8));
  LED led_19 (.in(puntajerecord_1_led9));
  LED led_20 (.in(puntajerecord_1_led10));
  DetectorFilaCompleta detectorfilacompleta_1 (
    .COL0(guardarnuevoestado_1_col_0), .COL1(guardarnuevoestado_1_col_1), .COL2(guardarnuevoestado_1_col_2),
    .COL3(guardarnuevoestado_1_col_3), .COL4(guardarnuevoestado_1_col_4),
    .BORRAR(detectorfilacompleta_1_borrar), .nuevaCol0(detectorfilacompleta_1_nuevacol0),
    .nuevaCol1(detectorfilacompleta_1_nuevacol1), .nuevaCol2(detectorfilacompleta_1_nuevacol2),
    .nuevaCol3(detectorfilacompleta_1_nuevacol3), .nuevaCol4(detectorfilacompleta_1_nuevacol4));
  and and_1 (and_1_out, Reloj, finpartida_1_fin);
  PuntajeRecord puntajerecord_1 (
    .LedEntrada1(contadorbin_1_led1), .LedEntrada2(contadorbin_1_led2), .LedEntrada3(contadorbin_1_led3),
    .LedEntrada4(contadorbin_1_led4), .LedEntrada5(contadorbin_1_led5), .LedEntrada6(contadorbin_1_led6),
    .LedEntrada7(contadorbin_1_led7), .LedEntrada8(contadorbin_1_led8), .LedEntrada9(contadorbin_1_led9),
    .LedEntrada10(contadorbin_1_led10), .ResetRecord(Reset_Record_out), .Clock(Reloj),
    .Led1(puntajerecord_1_led1), .Led2(puntajerecord_1_led2), .Led3(puntajerecord_1_led3),
    .Led4(puntajerecord_1_led4), .Led5(puntajerecord_1_led5), .Led6(puntajerecord_1_led6),
    .Led7(puntajerecord_1_led7), .Led8(puntajerecord_1_led8), .Led9(puntajerecord_1_led9),
    .Led10(puntajerecord_1_led10));
  juntarTableros juntartableros_1 (
    .blink(and_1_out), .GNE_C0(guardarnuevoestado_1_col_0), .MC_C0(movimientocuadrado_1_col0),
    .colLlena_0(finpartida_1_col0_full), .GNE_C1(guardarnuevoestado_1_col_1),
    .MC_C1(movimientocuadrado_1_col1), .colLlena_1(finpartida_1_col1_full),
    .GNE_C2(guardarnuevoestado_1_col_2), .MC_C2(movimientocuadrado_1_col2),
    .MC_C3(movimientocuadrado_1_col3), .GNE_C3(guardarnuevoestado_1_col_3),
    .colLlena_2(finpartida_1_col2_full), .MC_C4(movimientocuadrado_1_col4),
    .GNE_C4(guardarnuevoestado_1_col_4), .colLlena_3(finpartida_1_col3_full),
    .colLlena_4(finpartida_1_col4_full), .C0(juntartableros_1_c0), .C1(juntartableros_1_c1),
    .C2(juntartableros_1_c2), .C3(juntartableros_1_c3), .C4(juntartableros_1_c4));

  // Notes on the sheet:
  //   Configurar el reloj en 16 Hz
  //   Borrar puntaje actual: Tocar boton Reset
  //   Borrar puntaje record: Tocar boton Reset_Record
  //   Las velocidades de juego se manejan solas:
  //   - velocidad 1: menos de 400 bloques colocados
  //   - velocidad 2: entre 400 y 900 bloques colocados
  //   - velocidad 3: mas de 900 bloques colocados
  //   Para iniciar el juego: Mantener durante unos segundos el boton Start
  //   Movimiento: mover bloque a la derecha boton D, mover bloque a la izquierda boton I
  //   DECIMAL
  //   PUNTAJE ACTUAL
  //   BINARIO
  //   DECIMAL
  //   PUNTAJE RECORD
  //   BINARIO
endmodule

module contadorBin (
  input  Entrada,
  input  Suma5,
  input  Reset,
  input  Clock,
  output Led1,
  output Led2,
  output Led3,
  output Led4,
  output Led5,
  output Led6,
  output Led7,
  output Led8,
  output Led9,
  output Led10
);

  wire and_1_out, and_2_out, and_3_out, and_4_out, and_5_out, and_6_out, and_7_out, and_8_out, and_9_out,
       decoder_1_out1, decoder_1_out3, decoder_1_out5, decoder_1_out7, decoder_1_out9, decoder_1_out10,
       not_1_out, or_1_out, or_2_out, or_3_out;
  wire [3:0] counter_1_q;

  Counter #(.max('ha), .width(4)) counter_1 (
    .D(4'b1010), .Q(counter_1_q), .up(Entrada), .clk(or_1_out));  // open: load, count, carry, clr
  or or_1 (or_1_out, Suma5, and_1_out);
  and and_1 (and_1_out, Clock, not_1_out);
  Decoder #(.select(4)) decoder_1 (
    .out1(decoder_1_out1), .out3(decoder_1_out3), .out5(decoder_1_out5), .out7(decoder_1_out7),
    .out9(decoder_1_out9), .out10(decoder_1_out10), .sel(counter_1_q));  // open: out0, out2, out4, out6, out8, out11, out12, out13, out14, out15, en
  not not_1 (not_1_out, decoder_1_out10);
  or or_2 (or_2_out, decoder_1_out1, decoder_1_out3, decoder_1_out5, decoder_1_out7, decoder_1_out9);
  or or_3 (or_3_out, or_2_out, Entrada);
  J_K_Flip_Flop j_k_ff_1 (.J(or_3_out), .K(or_3_out), .clk(or_3_out), .Q(Led1), .reset(Reset));  // open: Qn, preset
  and and_2 (and_2_out, Led1, Led2);
  J_K_Flip_Flop j_k_ff_2 (.J(Led1), .K(Led1), .clk(or_3_out), .Q(Led2), .reset(Reset));  // open: Qn, preset
  and and_3 (and_3_out, and_2_out, Led3);
  J_K_Flip_Flop j_k_ff_3 (.J(and_2_out), .K(and_2_out), .clk(or_3_out), .Q(Led3), .reset(Reset));  // open: Qn, preset
  J_K_Flip_Flop j_k_ff_4 (.J(and_3_out), .K(and_3_out), .clk(or_3_out), .Q(Led4), .reset(Reset));  // open: Qn, preset
  and and_4 (and_4_out, and_3_out, Led4);
  J_K_Flip_Flop j_k_ff_5 (.J(and_4_out), .K(and_4_out), .clk(or_3_out), .Q(Led5), .reset(Reset));  // open: Qn, preset
  and and_5 (and_5_out, and_4_out, Led5);
  and and_6 (and_6_out, and_5_out, Led6);
  J_K_Flip_Flop j_k_ff_6 (.J(and_5_out), .K(and_5_out), .clk(or_3_out), .Q(Led6), .reset(Reset));  // open: Qn, preset
  J_K_Flip_Flop j_k_ff_7 (.J(and_6_out), .K(and_6_out), .clk(or_3_out), .Q(Led7), .reset(Reset));  // open: Qn, preset
  and and_7 (and_7_out, and_6_out, Led7);
  and and_8 (and_8_out, and_7_out, Led8);
  J_K_Flip_Flop j_k_ff_8 (.J(and_7_out), .K(and_7_out), .clk(or_3_out), .Q(Led8), .reset(Reset));  // open: Qn, preset
  J_K_Flip_Flop j_k_ff_9 (.J(and_8_out), .K(and_8_out), .clk(or_3_out), .Q(Led9), .reset(Reset));  // open: Qn, preset
  and and_9 (and_9_out, and_8_out, Led9);
  J_K_Flip_Flop j_k_ff_10 (.J(and_9_out), .K(and_9_out), .clk(or_3_out), .Q(Led10), .reset(Reset));  // open: Qn, preset
endmodule

module contador2 (
  input  Reset,
  input  Suma5,
  input  Sumar1,
  input  Clock,
  output [3:0] Puntos4,
  output [3:0] Puntos3,
  output [3:0] Puntos2,
  output [3:0] Puntos1
);

  wire and_1_out, counter_3_carry, counter_4_carry, counter_5_carry, decoder_1_out1, decoder_1_out3,
       decoder_1_out5, decoder_1_out7, decoder_1_out9, decoder_1_out10, not_1_out, not_2_out, not_3_out,
       not_4_out, or_1_out, or_2_out, or_3_out;
  wire [3:0] counter_1_q;

  Counter #(.max('ha), .width(4)) counter_1 (
    .D(4'b1010), .Q(counter_1_q), .up(Sumar1), .clk(or_1_out));  // open: load, count, carry, clr
  or or_1 (or_1_out, Suma5, and_1_out);
  and and_1 (and_1_out, Clock, not_1_out);
  Decoder #(.select(4)) decoder_1 (
    .out1(decoder_1_out1), .out3(decoder_1_out3), .out5(decoder_1_out5), .out7(decoder_1_out7),
    .out9(decoder_1_out9), .out10(decoder_1_out10), .sel(counter_1_q));  // open: out0, out2, out4, out6, out8, out11, out12, out13, out14, out15, en
  not not_1 (not_1_out, decoder_1_out10);
  or or_2 (or_2_out, decoder_1_out1, decoder_1_out3, decoder_1_out5, decoder_1_out7, decoder_1_out9);
  Counter #(.max('h9), .width(4)) counter_2 (
    .clr(Reset), .clk(not_2_out), .Q(Puntos4));  // open: load, up, count, D, carry
  Counter #(.max('h9), .width(4)) counter_3 (
    .clr(Reset), .clk(not_3_out), .carry(counter_3_carry), .Q(Puntos3));  // open: load, up, count, D
  Counter #(.max('h9), .width(4)) counter_4 (
    .clr(Reset), .clk(not_4_out), .carry(counter_4_carry), .Q(Puntos2));  // open: load, up, count, D
  Counter #(.max('h9), .width(4)) counter_5 (
    .clr(Reset), .clk(or_3_out), .carry(counter_5_carry), .Q(Puntos1));  // open: load, up, count, D
  or or_3 (or_3_out, or_2_out, Sumar1);
  not not_2 (not_2_out, counter_3_carry);
  not not_3 (not_3_out, counter_4_carry);
  not not_4 (not_4_out, counter_5_carry);
endmodule

module PuntajeRecord (
  input  LedEntrada1,
  input  LedEntrada2,
  input  LedEntrada3,
  input  LedEntrada4,
  input  LedEntrada5,
  input  LedEntrada6,
  input  LedEntrada7,
  input  LedEntrada8,
  input  LedEntrada9,
  input  LedEntrada10,
  input  ResetRecord,
  input  Clock,
  output Led1,
  output Led2,
  output Led3,
  output Led4,
  output Led5,
  output Led6,
  output Led7,
  output Led8,
  output Led9,
  output Led10
);

  wire and_1_out, comparator_1_gt;
  wire [9:0] d_ff_18_q;

  D_Flip_Flop d_ff_1 (.D(LedEntrada10), .clk(Clock), .Q(d_ff_18_q[9]));  // open: Qn, preset, reset
  D_Flip_Flop d_ff_2 (.D(LedEntrada9), .clk(Clock), .Q(d_ff_18_q[8]));  // open: Qn, preset, reset
  D_Flip_Flop d_ff_3 (.D(d_ff_18_q[9]), .clk(and_1_out), .Q(Led10), .reset(ResetRecord));  // open: Qn, preset
  D_Flip_Flop d_ff_4 (.D(LedEntrada8), .clk(Clock), .Q(d_ff_18_q[7]));  // open: Qn, preset, reset
  D_Flip_Flop d_ff_5 (.D(d_ff_18_q[8]), .clk(and_1_out), .Q(Led9), .reset(ResetRecord));  // open: Qn, preset
  D_Flip_Flop d_ff_6 (.D(LedEntrada7), .clk(Clock), .Q(d_ff_18_q[6]));  // open: Qn, preset, reset
  D_Flip_Flop d_ff_7 (.D(d_ff_18_q[7]), .clk(and_1_out), .Q(Led8), .reset(ResetRecord));  // open: Qn, preset
  D_Flip_Flop d_ff_8 (.D(LedEntrada6), .clk(Clock), .Q(d_ff_18_q[5]));  // open: Qn, preset, reset
  D_Flip_Flop d_ff_9 (.D(d_ff_18_q[6]), .clk(and_1_out), .Q(Led7), .reset(ResetRecord));  // open: Qn, preset
  D_Flip_Flop d_ff_10 (.D(LedEntrada5), .clk(Clock), .Q(d_ff_18_q[4]));  // open: Qn, preset, reset
  D_Flip_Flop d_ff_11 (.D(d_ff_18_q[5]), .clk(and_1_out), .Q(Led6), .reset(ResetRecord));  // open: Qn, preset
  D_Flip_Flop d_ff_12 (.D(LedEntrada4), .clk(Clock), .Q(d_ff_18_q[3]));  // open: Qn, preset, reset
  D_Flip_Flop d_ff_13 (.D(d_ff_18_q[4]), .clk(and_1_out), .Q(Led5), .reset(ResetRecord));  // open: Qn, preset
  D_Flip_Flop d_ff_14 (.D(LedEntrada3), .clk(Clock), .Q(d_ff_18_q[2]));  // open: Qn, preset, reset
  D_Flip_Flop d_ff_15 (.D(d_ff_18_q[3]), .clk(and_1_out), .Q(Led4), .reset(ResetRecord));  // open: Qn, preset
  Comparator #(.mode("unsigned"), .width(10)) comparator_1 (
    .a(d_ff_18_q), .b({Led10, Led9, Led8, Led7, Led6, Led5, Led4, Led3, Led2, Led1}), .gt(comparator_1_gt));  // open: eq, lt
  D_Flip_Flop d_ff_16 (.D(d_ff_18_q[2]), .clk(and_1_out), .Q(Led3), .reset(ResetRecord));  // open: Qn, preset
  D_Flip_Flop d_ff_17 (.D(LedEntrada2), .clk(Clock), .Q(d_ff_18_q[1]));  // open: Qn, preset, reset
  D_Flip_Flop d_ff_18 (.D(LedEntrada1), .clk(Clock), .Q(d_ff_18_q[0]));  // open: Qn, preset, reset
  D_Flip_Flop d_ff_19 (.D(d_ff_18_q[1]), .clk(and_1_out), .Q(Led2), .reset(ResetRecord));  // open: Qn, preset
  D_Flip_Flop d_ff_20 (.D(d_ff_18_q[0]), .clk(and_1_out), .Q(Led1), .reset(ResetRecord));  // open: Qn, preset
  and and_1 (and_1_out, comparator_1_gt, Clock);
endmodule

module PuntajeRecordHexa (
  input  [3:0] Puntos4,
  input  [3:0] Puntos3,
  input  [3:0] Puntos2,
  input  [3:0] Puntos1,
  input  Reset,
  input  Clock,
  output [3:0] Record4,
  output [3:0] Record3,
  output [3:0] Record2,
  output [3:0] Record1
);

  wire and_1_out, and_2_out, and_3_out, comparator_1_eq, comparator_1_gt, comparator_2_eq, comparator_2_gt,
       comparator_3_eq, comparator_3_gt, comparator_4_gt, or_1_out;

  Register #(.width(4)) register_1 (.D(Puntos4), .en(or_1_out), .clk(Clock), .Q(Record4), .clr(Reset));
  Register #(.width(4)) register_2 (.D(Puntos3), .en(or_1_out), .clk(Clock), .Q(Record3));  // open: clr
  Register #(.width(4)) register_3 (.D(Puntos2), .en(or_1_out), .clk(Clock), .Q(Record2), .clr(Reset));
  Register #(.width(4)) register_4 (.D(Puntos1), .en(or_1_out), .clk(Clock), .Q(Record1), .clr(Reset));
  Comparator #(.mode("unsigned"), .width(4)) comparator_1 (
    .a(Puntos4), .b(Record4), .gt(comparator_1_gt), .eq(comparator_1_eq));  // open: lt
  Comparator #(.mode("unsigned"), .width(4)) comparator_2 (
    .a(Puntos3), .b(Record3), .gt(comparator_2_gt), .eq(comparator_2_eq));  // open: lt
  Comparator #(.mode("unsigned"), .width(4)) comparator_3 (
    .a(Puntos2), .b(Record2), .gt(comparator_3_gt), .eq(comparator_3_eq));  // open: lt
  Comparator #(.mode("unsigned"), .width(4)) comparator_4 (
    .a(Puntos1), .b(Record1), .gt(comparator_4_gt));  // open: eq, lt
  and and_1 (and_1_out, comparator_1_eq, comparator_2_gt);
  and and_2 (and_2_out, comparator_1_eq, comparator_2_eq, comparator_3_gt);
  and and_3 (and_3_out, comparator_1_eq, comparator_2_eq, comparator_3_eq, comparator_4_gt);
  or or_1 (or_1_out, comparator_1_gt, and_1_out, and_2_out, and_3_out);
endmodule

module movimientoCuadrado (
  input  colisionY,
  input  strart,
  input  Clock,
  input  izq,
  input  der,
  input  colisionIzq,
  input  colisionDer,
  input  reset,
  output [4:0] inicio,
  output [7:0] col0,
  output [7:0] col1,
  output [7:0] col2,
  output [7:0] col3,
  output [7:0] col4,
  output [7:0] filaActual,
  output [2:0] colActual
);

  wire and_1_out, and_2_out, and_3_out, and_4_out, and_5_out, and_6_out, and_7_out, and_8_out, and_9_out,
       button_1_out, comparator_1_gt, comparator_2_eq, d_ff_1_q, d_ff_2_q, decoder_2_out0, decoder_2_out1,
       decoder_2_out2, decoder_2_out3, decoder_2_out4, not_1_out, not_2_out, not_3_out, not_4_out, not_5_out,
       not_6_out, not_7_out, not_8_out, not_9_out, not_10_out, or_1_out, or_2_out, or_3_out, or_4_out,
       or_5_out, or_6_out, or_7_out, or_8_out, or_9_out, or_10_out, or_11_out, or_12_out,
       shift_register_2_out, shift_register_3_out, shift_register_4_out, shift_register_5_out,
       shift_register_6_out;
  wire [2:0] undriven;
  wire [7:0] shift_register_1_q7;

  Decoder #(.select(3)) decoder_1 (
    .out0(inicio[0]), .out1(inicio[3]), .out2(inicio[2]), .out3(inicio[1]), .out4(inicio[4]), .sel(undriven));  // open: out5, out6, out7, en
  DotMatrix #(.matrixrows(1)) dotmatrix_1 (
    .col0(inicio[0]), .col1(inicio[3]), .col2(inicio[2]), .col3(inicio[1]), .col4(inicio[4]));
  DotMatrix #(.matrixrows(8)) dotmatrix_2 (.col0(col0), .col1(col1), .col2(col2), .col3(col3), .col4(col4));
  Button button_1 (.out(button_1_out));
  or or_1 (or_1_out, strart, button_1_out);
  D_Flip_Flop d_ff_1 (.D(or_1_out), .clk(Clock), .Q(d_ff_1_q));  // open: Qn, preset, reset
  or or_2 (or_2_out, not_1_out, comparator_2_eq);
  not not_1 (not_1_out, comparator_1_gt);
  and and_1 (and_1_out, not_2_out, izq);
  not not_2 (not_2_out, colisionIzq);
  not not_3 (not_3_out, colisionY);
  Random #(.width(3)) random_1 ();  // open: clk, next, out, clr
  and and_2 (and_2_out, or_2_out, not_5_out);
  Comparator #(.mode("unsigned"), .width(3)) comparator_1 (
    .a(3'b101), .b(undriven), .gt(comparator_1_gt));  // open: eq, lt
  and and_3 (and_3_out, comparator_1_gt, or_5_out);
  Counter #(.max('h4), .ongoal("stay"), .width(3)) counter_1 (
    .load(and_3_out), .D(undriven), .count(or_4_out), .Q(colActual), .up(and_4_out), .clk(or_3_out));  // open: carry, clr
  or or_3 (or_3_out, and_3_out, or_4_out);
  or or_4 (or_4_out, and_1_out, and_4_out);
  and and_4 (and_4_out, der, not_4_out);
  Comparator #(.mode("unsigned")) comparator_2 (
    .a(shift_register_1_q7), .b(8'h40), .eq(comparator_2_eq));  // open: gt, lt
  Decoder #(.select(3)) decoder_2 (
    .out0(decoder_2_out0), .out1(decoder_2_out1), .out2(decoder_2_out2), .out3(decoder_2_out3),
    .out4(decoder_2_out4), .sel(colActual));  // open: out5, out6, out7, en
  not not_4 (not_4_out, colisionDer);
  not not_5 (not_5_out, Clock);
  or or_5 (or_5_out, d_ff_2_q, d_ff_1_q);
  Shift_Register shift_register_1 (
    .shift(not_3_out), .in(1'b0), .clk(Clock), .load(or_5_out), .clr(reset), .d0(1'b1),
    .q0(shift_register_1_q7[7]), .d1(1'b0), .q1(shift_register_1_q7[6]), .d2(1'b0),
    .q2(shift_register_1_q7[5]), .d3(1'b0), .q3(shift_register_1_q7[4]), .d4(1'b0),
    .q4(shift_register_1_q7[3]), .d5(1'b0), .q5(shift_register_1_q7[2]), .d6(1'b0),
    .q6(shift_register_1_q7[1]), .d7(1'b0), .q7(shift_register_1_q7[0]));  // open: out
  and and_5 (and_5_out, not_5_out, decoder_2_out0);
  and and_6 (and_6_out, not_5_out, decoder_2_out1);
  and and_7 (and_7_out, not_5_out, decoder_2_out2);
  and and_8 (and_8_out, not_5_out, decoder_2_out3);
  and and_9 (and_9_out, not_5_out, decoder_2_out4);
  not not_6 (not_6_out, decoder_2_out0);
  not not_7 (not_7_out, decoder_2_out1);
  not not_8 (not_8_out, decoder_2_out2);
  not not_9 (not_9_out, decoder_2_out3);
  not not_10 (not_10_out, decoder_2_out4);
  D_Flip_Flop d_ff_2 (.D(or_6_out), .clk(Clock), .Q(d_ff_2_q));  // open: Qn, preset, reset
  or or_6 (or_6_out, colisionY, or_12_out);
  or or_7 (or_7_out, not_6_out, or_5_out);
  or or_8 (or_8_out, not_7_out, or_5_out);
  or or_9 (or_9_out, not_8_out, or_5_out);
  or or_10 (or_10_out, not_9_out, or_5_out);
  or or_11 (or_11_out, not_10_out, or_5_out);
  Shift_Register shift_register_2 (
    .clk(and_5_out), .out(shift_register_2_out), .load(and_5_out), .clr(or_7_out),
    .d0(shift_register_1_q7[7]), .q0(col0[7]), .d1(shift_register_1_q7[6]), .q1(col0[6]),
    .d2(shift_register_1_q7[5]), .q2(col0[5]), .d3(shift_register_1_q7[4]), .q3(col0[4]),
    .d4(shift_register_1_q7[3]), .q4(col0[3]), .d5(shift_register_1_q7[2]), .q5(col0[2]),
    .d6(shift_register_1_q7[1]), .q6(col0[1]), .d7(shift_register_1_q7[0]), .q7(col0[0]));  // open: shift, in
  Shift_Register shift_register_3 (
    .clk(and_6_out), .out(shift_register_3_out), .load(and_6_out), .clr(or_8_out),
    .d0(shift_register_1_q7[7]), .q0(col1[7]), .d1(shift_register_1_q7[6]), .q1(col1[6]),
    .d2(shift_register_1_q7[5]), .q2(col1[5]), .d3(shift_register_1_q7[4]), .q3(col1[4]),
    .d4(shift_register_1_q7[3]), .q4(col1[3]), .d5(shift_register_1_q7[2]), .q5(col1[2]),
    .d6(shift_register_1_q7[1]), .q6(col1[1]), .d7(shift_register_1_q7[0]), .q7(col1[0]));  // open: shift, in
  Shift_Register shift_register_4 (
    .clk(and_7_out), .out(shift_register_4_out), .load(and_7_out), .clr(or_9_out),
    .d0(shift_register_1_q7[7]), .q0(col2[7]), .d1(shift_register_1_q7[6]), .q1(col2[6]),
    .d2(shift_register_1_q7[5]), .q2(col2[5]), .d3(shift_register_1_q7[4]), .q3(col2[4]),
    .d4(shift_register_1_q7[3]), .q4(col2[3]), .d5(shift_register_1_q7[2]), .q5(col2[2]),
    .d6(shift_register_1_q7[1]), .q6(col2[1]), .d7(shift_register_1_q7[0]), .q7(col2[0]));  // open: shift, in
  Shift_Register shift_register_5 (
    .clk(and_8_out), .out(shift_register_5_out), .load(and_8_out), .clr(or_10_out),
    .d0(shift_register_1_q7[7]), .q0(col3[7]), .d1(shift_register_1_q7[6]), .q1(col3[6]),
    .d2(shift_register_1_q7[5]), .q2(col3[5]), .d3(shift_register_1_q7[4]), .q3(col3[4]),
    .d4(shift_register_1_q7[3]), .q4(col3[3]), .d5(shift_register_1_q7[2]), .q5(col3[2]),
    .d6(shift_register_1_q7[1]), .q6(col3[1]), .d7(shift_register_1_q7[0]), .q7(col3[0]));  // open: shift, in
  Shift_Register shift_register_6 (
    .clk(and_9_out), .out(shift_register_6_out), .load(and_9_out), .clr(or_11_out),
    .d0(shift_register_1_q7[7]), .q0(col4[7]), .d1(shift_register_1_q7[6]), .q1(col4[6]),
    .d2(shift_register_1_q7[5]), .q2(col4[5]), .d3(shift_register_1_q7[4]), .q3(col4[4]),
    .d4(shift_register_1_q7[3]), .q4(col4[3]), .d5(shift_register_1_q7[2]), .q5(col4[2]),
    .d6(shift_register_1_q7[1]), .q6(col4[1]), .d7(shift_register_1_q7[0]), .q7(col4[0]));  // open: shift, in
  or or_12 (or_12_out, shift_register_2_out, shift_register_3_out, shift_register_4_out, shift_register_5_out, shift_register_6_out);
  Multiplexer #(.select(3), .width(8)) multiplexer_1 (
    .in0(col0), .in1(col1), .in2(col2), .in3(col3), .in4(col4), .out(filaActual), .sel(colActual));  // open: in5, in6, in7
endmodule

module guardarNuevoEstado (
  input  BORRAR_FILA,
  input  CLK,
  input  RESET,
  input  WRITE_ENABLE,
  input  [7:0] Y_POS,
  input  [2:0] X_POS,
  input  [7:0] LOOP_C0,
  input  [7:0] LOOP_C1,
  input  [7:0] LOOP_C2,
  input  [7:0] LOOP_C3,
  input  [7:0] LOOP_C4,
  output [7:0] COL_0,
  output [7:0] COL_1,
  output [7:0] COL_2,
  output [7:0] COL_3,
  output [7:0] COL_4,
  output colisionY,
  output colisionDer,
  output colisionIzq,
  output SumarPunto
);

  wire and_1_out, and_2_out, and_3_out, and_4_out, and_5_out, and_6_out, and_7_out, and_8_out, and_9_out,
       and_10_out, comparator_1_gt, comparator_2_gt, comparator_3_gt, comparator_4_gt, comparator_5_gt,
       comparator_7_eq, comparator_8_gt, decoder_1_out0, decoder_1_out1, decoder_1_out2, decoder_1_out3,
       decoder_1_out4, not_1_out, or_1_out, or_2_out;
  wire [2:0] REG_X_q;
  wire [4:0] decoder_2_out0;
  wire [7:0] adder_1_out, multiplexer_1_out, REG_Y_q;

  and and_1 (and_1_out, 1'b1, colisionY);
  Register REG_Y (.D(Y_POS), .en(and_1_out), .clk(CLK), .Q(REG_Y_q), .clr(RESET));
  Register #(.width(3)) REG_X (.D(X_POS), .en(and_1_out), .clk(CLK), .Q(REG_X_q), .clr(RESET));
  Comparator #(.mode("unsigned")) comparator_1 (.a(COL_0), .b(Y_POS), .gt(comparator_1_gt));  // open: eq, lt
  Comparator #(.mode("unsigned")) comparator_2 (.a(COL_1), .b(Y_POS), .gt(comparator_2_gt));  // open: eq, lt
  Comparator #(.mode("unsigned")) comparator_3 (.a(COL_2), .b(Y_POS), .gt(comparator_3_gt));  // open: eq, lt
  Comparator #(.mode("unsigned")) comparator_4 (.a(COL_3), .b(Y_POS), .gt(comparator_4_gt));  // open: eq, lt
  Comparator #(.mode("unsigned")) comparator_5 (.a(COL_4), .b(Y_POS), .gt(comparator_5_gt));  // open: eq, lt
  Comparator #(.mode("unsigned")) comparator_6 (.a(Y_POS), .b(8'h3));  // open: gt, eq, lt
  Decoder #(.select(3)) decoder_1 (
    .out0(decoder_1_out0), .out1(decoder_1_out1), .out2(decoder_1_out2), .out3(decoder_1_out3),
    .out4(decoder_1_out4), .sel(X_POS));  // open: out5, out6, out7, en
  Decoder #(.select(3)) decoder_2 (
    .out0(decoder_2_out0[0]), .out1(decoder_2_out0[1]), .out2(decoder_2_out0[2]), .out3(decoder_2_out0[3]),
    .out4(decoder_2_out0[4]), .sel(REG_X_q), .en(1'b1));  // open: out5, out6, out7
  and and_2 (and_2_out, decoder_1_out0, comparator_2_gt);
  and and_3 (and_3_out, decoder_1_out1, comparator_3_gt);
  and and_4 (and_4_out, decoder_1_out2, comparator_4_gt);
  and and_5 (and_5_out, decoder_1_out3, comparator_5_gt);
  or or_1 (or_1_out, and_2_out, and_3_out, and_4_out, and_5_out);
  D_Flip_Flop d_ff_1 (.D(or_1_out), .clk(WRITE_ENABLE), .Q(colisionDer));  // open: Qn, preset, reset
  and and_6 (and_6_out, comparator_1_gt, decoder_1_out1);
  and and_7 (and_7_out, comparator_2_gt, decoder_1_out2);
  and and_8 (and_8_out, comparator_3_gt, decoder_1_out3);
  and and_9 (and_9_out, comparator_4_gt, decoder_1_out4);
  registrosColumnas registroscolumnas_1 (
    .WRITE(and_1_out), .INPUT_BORRAR(LOOP_C0), .BORRAR_FILA(BORRAR_FILA), .REG_Y(REG_Y_q),
    .REG_X(decoder_2_out0[0]), .CLOCK(CLK), .RESET(RESET), .COL(COL_0));
  D_Flip_Flop d_ff_2 (.D(or_2_out), .clk(WRITE_ENABLE), .Q(colisionIzq));  // open: Qn, preset, reset
  or or_2 (or_2_out, and_6_out, and_7_out, and_8_out, and_9_out);
  Multiplexer #(.select(3), .width(8)) multiplexer_1 (
    .in0(COL_0), .in1(COL_1), .in2(COL_2), .in3(COL_3), .in4(COL_4), .out(multiplexer_1_out), .sel(X_POS));  // open: in5, in6, in7
  registrosColumnas registroscolumnas_2 (
    .WRITE(and_1_out), .INPUT_BORRAR(LOOP_C1), .BORRAR_FILA(BORRAR_FILA), .REG_Y(REG_Y_q),
    .REG_X(decoder_2_out0[1]), .CLOCK(CLK), .RESET(RESET), .COL(COL_1));
  Adder adder_1 (.a(multiplexer_1_out), .b(8'h1), .out(adder_1_out));  // open: cin, cout
  not not_1 (not_1_out, comparator_7_eq);
  Comparator #(.mode("unsigned")) comparator_7 (.a(Y_POS), .b({8{1'b0}}), .eq(comparator_7_eq));  // open: gt, lt
  Comparator #(.mode("unsigned")) comparator_8 (
    .a(adder_1_out), .b(Y_POS), .gt(comparator_8_gt), .eq(SumarPunto));  // open: lt
  and and_10 (and_10_out, not_1_out, comparator_8_gt);
  or or_3 (colisionY, and_10_out, SumarPunto);
  registrosColumnas registroscolumnas_3 (
    .WRITE(and_1_out), .INPUT_BORRAR(LOOP_C2), .BORRAR_FILA(BORRAR_FILA), .REG_Y(REG_Y_q),
    .REG_X(decoder_2_out0[2]), .CLOCK(CLK), .RESET(RESET), .COL(COL_2));
  registrosColumnas registroscolumnas_4 (
    .WRITE(and_1_out), .INPUT_BORRAR(LOOP_C3), .BORRAR_FILA(BORRAR_FILA), .REG_Y(REG_Y_q),
    .REG_X(decoder_2_out0[3]), .CLOCK(CLK), .RESET(RESET), .COL(COL_3));
  registrosColumnas registroscolumnas_5 (
    .WRITE(and_1_out), .INPUT_BORRAR(LOOP_C4), .BORRAR_FILA(BORRAR_FILA), .REG_Y(REG_Y_q),
    .REG_X(decoder_2_out0[4]), .CLOCK(CLK), .RESET(RESET), .COL(COL_4));

  // Other names for the same wires on the sheet: L_C0[7:0] = LOOP_C0; L_C1[7:0] = LOOP_C1; L_C2[7:0] = LOOP_C2;
  //   L_C3[7:0] = LOOP_C3; L_C4[7:0] = LOOP_C4
endmodule

module colisionesMemoria (
  input  [2:0] colActual,
  input  [7:0] filaActual
);

  wire clock_2_out, comparator_1_eq, comparator_2_eq;
  wire [7:0] ram_1_dout;

  Clock clock_1 ();  // open: out
  Comparator comparator_1 (.a(filaActual), .b(8'h1), .eq(comparator_1_eq));  // open: gt, lt
  Clock clock_2 (.out(clock_2_out));
  RAM #(.addrWidth(3)) ram_1 (
    .addr(colActual), .clk(clock_2_out), .din(filaActual), .dout(ram_1_dout));  // open: we, oe
  Comparator comparator_2 (.a(ram_1_dout), .b({8{1'b0}}), .eq(comparator_2_eq));  // open: gt, lt
endmodule

module DetectorFilaCompleta (
  input  [7:0] COL0,
  input  [7:0] COL1,
  input  [7:0] COL2,
  input  [7:0] COL3,
  input  [7:0] COL4,
  output BORRAR,
  output [7:0] nuevaCol0,
  output [7:0] nuevaCol1,
  output [7:0] nuevaCol2,
  output [7:0] nuevaCol3,
  output [7:0] nuevaCol4
);

  wire comparator_1_gt, comparator_2_gt, comparator_3_gt, comparator_4_gt, comparator_5_gt;
  wire [2:0] multiplexer_1_out;

  Comparator comparator_1 (.a(COL0), .b({8{1'b0}}), .gt(comparator_1_gt));  // open: eq, lt
  Comparator comparator_2 (.a(COL1), .b({8{1'b0}}), .gt(comparator_2_gt));  // open: eq, lt
  Comparator comparator_3 (.a(COL2), .b({8{1'b0}}), .gt(comparator_3_gt));  // open: eq, lt
  Comparator comparator_4 (.a(COL3), .b({8{1'b0}}), .gt(comparator_4_gt));  // open: eq, lt
  Comparator comparator_5 (.a(COL4), .b({8{1'b0}}), .gt(comparator_5_gt));  // open: eq, lt
  and and_1 (BORRAR, comparator_1_gt, comparator_2_gt, comparator_3_gt, comparator_4_gt, comparator_5_gt);
  Multiplexer #(.width(3)) multiplexer_1 (.in0(3'b000), .in1(3'b001), .out(multiplexer_1_out), .sel(BORRAR));
  Shifter #(.shift("lr")) shifter_1 (.in(COL0), .\dist (multiplexer_1_out), .out(nuevaCol0));
  Shifter #(.shift("lr")) shifter_2 (.in(COL1), .\dist (multiplexer_1_out), .out(nuevaCol1));
  Shifter #(.shift("lr")) shifter_3 (.in(COL2), .\dist (multiplexer_1_out), .out(nuevaCol2));
  Shifter #(.shift("lr")) shifter_4 (.in(COL3), .\dist (multiplexer_1_out), .out(nuevaCol3));
  Shifter #(.shift("lr")) shifter_5 (.in(COL4), .\dist (multiplexer_1_out), .out(nuevaCol4));
endmodule

module ReductorFrecuencia2 (
  input  Reloj,
  input  Activador,
  input  Reset,
  output RelojDividido
);

  wire and_1_out, not_1_out;

  and and_1 (and_1_out, Reloj, Activador);
  Register #(.width(1)) register_1 (.D(not_1_out), .en(1'b1), .clk(and_1_out), .Q(RelojDividido), .clr(Reset));
  not not_1 (not_1_out, RelojDividido);
endmodule

module ReductorFrecuencia4 (
  input  Reloj,
  input  Activador,
  input  Reset,
  output RelojDividido
);

  wire and_1_out, not_1_out, not_2_out, register_1_q;

  and and_1 (and_1_out, Reloj, Activador);
  Register #(.width(1)) register_1 (.D(not_1_out), .en(1'b1), .clk(and_1_out), .Q(register_1_q), .clr(Reset));
  not not_1 (not_1_out, register_1_q);
  Register #(.width(1)) register_2 (.D(not_2_out), .en(1'b1), .clk(register_1_q), .Q(RelojDividido), .clr(Reset));
  not not_2 (not_2_out, RelojDividido);
endmodule

module ReductorFrecuencia8 (
  input  Reloj,
  input  Activador,
  input  Reset,
  output RelojDividido
);

  wire and_1_out, not_1_out, not_2_out, not_3_out, register_1_q, register_2_q;

  and and_1 (and_1_out, Reloj, Activador);
  Register #(.width(1)) register_1 (.D(not_1_out), .en(1'b1), .clk(and_1_out), .Q(register_1_q), .clr(Reset));
  not not_1 (not_1_out, register_1_q);
  Register #(.width(1)) register_2 (.D(not_2_out), .en(1'b1), .clk(register_1_q), .Q(register_2_q), .clr(Reset));
  not not_2 (not_2_out, register_2_q);
  Register #(.width(1)) register_3 (.D(not_3_out), .en(1'b1), .clk(register_2_q), .Q(RelojDividido), .clr(Reset));
  not not_3 (not_3_out, RelojDividido);
endmodule

module NivelVelocidad (
  input  Entrada,
  input  Reset,
  output velocidad1,
  output velocidad2,
  output velocidad3
);

  wire comparator_1_eq, comparator_1_gt, comparator_1_lt, comparator_2_eq, comparator_2_gt, comparator_2_lt,
       or_1_out;
  wire [9:0] counter_1_q;

  Counter #(.max('h3ff), .ongoal("stay"), .width(10)) counter_1 (
    .Q(counter_1_q), .clk(Entrada), .clr(Reset));  // open: load, D, count, carry, up
  Comparator #(.mode("unsigned"), .width(10)) comparator_1 (
    .a(counter_1_q), .b(10'h190), .gt(comparator_1_gt), .eq(comparator_1_eq), .lt(comparator_1_lt));
  Comparator #(.mode("unsigned"), .width(10)) comparator_2 (
    .a(counter_1_q), .b(10'h384), .gt(comparator_2_gt), .eq(comparator_2_eq), .lt(comparator_2_lt));
  or or_1 (or_1_out, comparator_1_gt, comparator_1_eq);
  or or_2 (velocidad3, comparator_2_gt, comparator_2_eq);
  and and_1 (velocidad1, comparator_1_lt, comparator_2_lt);
  and and_2 (velocidad2, or_1_out, comparator_2_lt);
endmodule

module ManejoVelocidades (
  input  clk,
  input  entrada,
  input  reset,
  output salida
);

  wire nivelvelocidad_1_velocidad1, nivelvelocidad_1_velocidad2, nivelvelocidad_1_velocidad3, or_1_out,
       or_2_out, reductorfrecuencia4_1_relojdividido, reductorfrecuencia8_1_relojdividido,
       reductorfrecuencia8_2_relojdividido;

  NivelVelocidad nivelvelocidad_1 (
    .Entrada(entrada), .Reset(reset), .velocidad1(nivelvelocidad_1_velocidad1),
    .velocidad2(nivelvelocidad_1_velocidad2), .velocidad3(nivelvelocidad_1_velocidad3));
  or or_1 (or_1_out, nivelvelocidad_1_velocidad2, reset);
  or or_2 (or_2_out, nivelvelocidad_1_velocidad3, reset);
  ReductorFrecuencia8 reductorfrecuencia8_1 (
    .Reloj(clk), .Activador(nivelvelocidad_1_velocidad1), .Reset(or_1_out),
    .RelojDividido(reductorfrecuencia8_1_relojdividido));
  ReductorFrecuencia4 reductorfrecuencia4_1 (
    .Reloj(clk), .Activador(nivelvelocidad_1_velocidad2), .Reset(or_2_out),
    .RelojDividido(reductorfrecuencia4_1_relojdividido));
  ReductorFrecuencia8 reductorfrecuencia8_2 (
    .Reloj(clk), .Activador(nivelvelocidad_1_velocidad3), .Reset(reset),
    .RelojDividido(reductorfrecuencia8_2_relojdividido));
  or or_3 (salida, reductorfrecuencia8_1_relojdividido, reductorfrecuencia4_1_relojdividido, reductorfrecuencia8_2_relojdividido);
endmodule

module registrosColumnas (
  input  WRITE,
  input  [7:0] INPUT_BORRAR,
  input  BORRAR_FILA,
  input  [7:0] REG_Y,
  input  REG_X,
  input  CLOCK,
  input  RESET,
  output [7:0] COL
);

  wire and_1_out, or_2_out;
  wire [7:0] multiplexer_1_out, or_1_out;

  assign or_1_out = COL | REG_Y;  // OR_Gate or_1, 8 bits wide
  and and_1 (and_1_out, REG_X, WRITE);
  Multiplexer #(.width(8)) multiplexer_1 (
    .in0(or_1_out), .in1(INPUT_BORRAR), .out(multiplexer_1_out), .sel(BORRAR_FILA));
  or or_2 (or_2_out, BORRAR_FILA, and_1_out);
  Register register_1 (.D(multiplexer_1_out), .en(or_2_out), .Q(COL), .clk(CLOCK), .clr(RESET));
endmodule

module parpadeoColumna (
  input  CLOCK,
  input  FIN,
  input  RESET,
  input  COL0_FULL,
  input  COL1_FULL,
  input  COL2_FULL,
  input  COL3_FULL,
  input  COL4_FULL,
  input  [7:0] COL_0,
  input  [7:0] COL_1,
  input  [7:0] COL_2,
  input  [7:0] COL_3,
  input  [7:0] COL_4,
  output [7:0] BLINK_COL0,
  output [7:0] BLINK_COL1,
  output [7:0] BLINK_COL2,
  output [7:0] BLINK_COL3,
  output [7:0] BLINK_COL4
);

  wire and_1_out, and_2_out, and_3_out, and_4_out, and_5_out, and_6_out;
  wire [7:0] counter_1_q;

  Counter counter_1 (.count(1'b1), .Q(counter_1_q), .up(1'b1), .clk(CLOCK), .clr(RESET));  // open: load, D, carry
  and and_1 (and_1_out, counter_1_q[7], FIN);
  and and_2 (and_2_out, COL0_FULL, and_1_out);
  and and_3 (and_3_out, COL1_FULL, and_1_out);
  and and_4 (and_4_out, COL2_FULL, and_1_out);
  and and_5 (and_5_out, COL3_FULL, and_1_out);
  and and_6 (and_6_out, COL4_FULL, and_1_out);
  Multiplexer #(.width(8)) multiplexer_1 (.in0(COL_0), .in1({8{1'b0}}), .out(BLINK_COL0), .sel(and_2_out));
  Multiplexer #(.width(8)) multiplexer_2 (.in0(COL_1), .in1({8{1'b0}}), .out(BLINK_COL1), .sel(and_3_out));
  Multiplexer #(.width(8)) multiplexer_3 (.in0(COL_2), .in1({8{1'b0}}), .out(BLINK_COL2), .sel(and_4_out));
  Multiplexer #(.width(8)) multiplexer_4 (.in0(COL_3), .in1({8{1'b0}}), .out(BLINK_COL3), .sel(and_5_out));
  Multiplexer #(.width(8)) multiplexer_5 (.in0(COL_4), .in1({8{1'b0}}), .out(BLINK_COL4), .sel(and_6_out));
endmodule

module juntarTableros (
  input  blink,
  input  [7:0] GNE_C0,
  input  [7:0] MC_C0,
  input  colLlena_0,
  input  [7:0] GNE_C1,
  input  [7:0] MC_C1,
  input  colLlena_1,
  input  [7:0] GNE_C2,
  input  [7:0] MC_C2,
  input  [7:0] MC_C3,
  input  [7:0] GNE_C3,
  input  colLlena_2,
  input  [7:0] MC_C4,
  input  [7:0] GNE_C4,
  input  colLlena_3,
  input  colLlena_4,
  output [7:0] C0,
  output [7:0] C1,
  output [7:0] C2,
  output [7:0] C3,
  output [7:0] C4
);

  wire and_1_out, and_2_out, and_3_out, and_4_out, and_5_out;
  wire [7:0] multiplexer_1_out, multiplexer_2_out, multiplexer_3_out, multiplexer_4_out, multiplexer_5_out;

  assign C0 = MC_C0 ^ multiplexer_1_out;  // XOR_Gate xor_1, 8 bits wide
  assign C1 = MC_C1 ^ multiplexer_2_out;  // XOR_Gate xor_2, 8 bits wide
  assign C2 = MC_C2 ^ multiplexer_3_out;  // XOR_Gate xor_3, 8 bits wide
  assign C3 = MC_C3 ^ multiplexer_4_out;  // XOR_Gate xor_4, 8 bits wide
  assign C4 = MC_C4 ^ multiplexer_5_out;  // XOR_Gate xor_5, 8 bits wide
  Multiplexer #(.width(8)) multiplexer_1 (.in0(GNE_C0), .in1({8{1'b0}}), .out(multiplexer_1_out), .sel(and_1_out));
  Multiplexer #(.width(8)) multiplexer_2 (.in0(GNE_C1), .in1({8{1'b0}}), .out(multiplexer_2_out), .sel(and_2_out));
  Multiplexer #(.width(8)) multiplexer_3 (.in0(GNE_C2), .in1({8{1'b0}}), .out(multiplexer_3_out), .sel(and_3_out));
  Multiplexer #(.width(8)) multiplexer_4 (.in0(GNE_C3), .in1({8{1'b0}}), .out(multiplexer_4_out), .sel(and_4_out));
  Multiplexer #(.width(8)) multiplexer_5 (.in0(GNE_C4), .in1({8{1'b0}}), .out(multiplexer_5_out), .sel(and_5_out));
  and and_1 (and_1_out, blink, colLlena_0);
  and and_2 (and_2_out, blink, colLlena_1);
  and and_3 (and_3_out, blink, colLlena_2);
  and and_4 (and_4_out, blink, colLlena_3);
  and and_5 (and_5_out, blink, colLlena_4);
endmodule

module mergeTableros (
  input  blink,
  input  [7:0] GNE_C0,
  input  [7:0] MC_C0,
  input  colLlena_0,
  input  [7:0] GNE_C1,
  input  [7:0] MC_C1,
  input  colLlena_1,
  input  [7:0] GNE_C2,
  input  [7:0] MC_C2,
  input  [7:0] MC_C3,
  input  [7:0] GNE_C3,
  input  colLlena_2,
  input  [7:0] MC_C4,
  input  [7:0] GNE_C4,
  input  colLlena_3,
  input  colLlena_4,
  output [7:0] C0,
  output [7:0] C1,
  output [7:0] C2,
  output [7:0] C3,
  output [7:0] C4
);

  wire and_1_out, and_2_out, and_3_out, and_4_out, and_5_out;
  wire [7:0] multiplexer_1_out, multiplexer_2_out, multiplexer_3_out, multiplexer_4_out, multiplexer_5_out;

  assign C0 = MC_C0 ^ multiplexer_1_out;  // XOR_Gate xor_1, 8 bits wide
  assign C1 = MC_C1 ^ multiplexer_2_out;  // XOR_Gate xor_2, 8 bits wide
  assign C2 = MC_C2 ^ multiplexer_3_out;  // XOR_Gate xor_3, 8 bits wide
  assign C3 = MC_C3 ^ multiplexer_4_out;  // XOR_Gate xor_4, 8 bits wide
  assign C4 = MC_C4 ^ multiplexer_5_out;  // XOR_Gate xor_5, 8 bits wide
  Multiplexer #(.width(8)) multiplexer_1 (.in0(GNE_C0), .in1({8{1'b0}}), .out(multiplexer_1_out), .sel(and_1_out));
  Multiplexer #(.width(8)) multiplexer_2 (.in0(GNE_C1), .in1({8{1'b0}}), .out(multiplexer_2_out), .sel(and_2_out));
  Multiplexer #(.width(8)) multiplexer_3 (.in0(GNE_C2), .in1({8{1'b0}}), .out(multiplexer_3_out), .sel(and_3_out));
  Multiplexer #(.width(8)) multiplexer_4 (.in0(GNE_C3), .in1({8{1'b0}}), .out(multiplexer_4_out), .sel(and_4_out));
  Multiplexer #(.width(8)) multiplexer_5 (.in0(GNE_C4), .in1({8{1'b0}}), .out(multiplexer_5_out), .sel(and_5_out));
  and and_1 (and_1_out, blink, colLlena_0);
  and and_2 (and_2_out, blink, colLlena_1);
  and and_3 (and_3_out, blink, colLlena_2);
  and and_4 (and_4_out, blink, colLlena_3);
  and and_5 (and_5_out, blink, colLlena_4);
endmodule

module finPartida (
  input  clk,
  input  [7:0] col0,
  input  [7:0] col1,
  input  [7:0] col2,
  input  [7:0] col3,
  input  [7:0] col4,
  output reset,
  output fin,
  output COL0_FULL,
  output COL1_FULL,
  output COL2_FULL,
  output COL3_FULL,
  output COL4_FULL
);

  wire comparator_6_eq, not_1_out, or_1_out;
  wire [3:0] counter_1_q;

  Comparator comparator_1 (.a(col0), .b({8{1'b1}}), .eq(COL0_FULL));  // open: gt, lt
  Comparator comparator_2 (.a(col1), .b({8{1'b1}}), .eq(COL1_FULL));  // open: gt, lt
  Comparator comparator_3 (.a(col2), .b({8{1'b1}}), .eq(COL2_FULL));  // open: gt, lt
  Comparator comparator_4 (.a(col3), .b({8{1'b1}}), .eq(COL3_FULL));  // open: gt, lt
  Comparator comparator_5 (.a(col4), .b({8{1'b1}}), .eq(COL4_FULL));  // open: gt, lt
  or or_1 (or_1_out, fin, not_1_out);
  or or_2 (fin, COL0_FULL, COL1_FULL, COL2_FULL, COL3_FULL, COL4_FULL);
  Counter #(.max('hf), .width(4)) counter_1 (
    .count(or_1_out), .Q(counter_1_q), .clk(clk));  // open: load, D, carry, up, clr
  Comparator #(.width(4)) comparator_6 (.a(counter_1_q), .b(4'b0000), .eq(comparator_6_eq));  // open: gt, lt
  not not_1 (not_1_out, comparator_6_eq);
  Comparator #(.width(4)) comparator_7 (.a(counter_1_q), .b(4'b1010), .eq(reset));  // open: gt, lt
endmodule
